// Logisim project lab04.circ as structural Verilog: 1 circuit, main circuit main
module main (
  input  DOWN_UP,
  input  nENABLE,
  input  ABCD
);

  wire button_1_out, clock_1_out, l_74155_decoder_1_p1, l_74155_decoder_1_p5, l_74155_decoder_1_p6,
       l_74155_decoder_1_p7, l_74155_decoder_1_p8, l_74155_decoder_1_p9, l_74155_decoder_1_p10,
       l_74155_decoder_1_p11, l_74155_decoder_1_p12, l_74155_decoder_1_p13, l_74155_decoder_1_p14,
       l_74191_counter_1_p4;

  // L_74155_decoder l_74155_decoder_1: pin names not known; wires that end beside it: l_74155_decoder_1_p1, l_74155_decoder_1_p1, nENABLE, nENABLE, l_74155_decoder_1_p5, l_74155_decoder_1_p6, l_74155_decoder_1_p7, l_74155_decoder_1_p8, l_74155_decoder_1_p9, l_74155_decoder_1_p10, l_74155_decoder_1_p11, l_74155_decoder_1_p12, l_74155_decoder_1_p13, l_74155_decoder_1_p14
  Clock clock_1 (.out(clock_1_out));
  // L_74191_counter l_74191_counter_1: pin names not known; wires that end beside it: ABCD, ABCD, l_74155_decoder_1_p1, l_74191_counter_1_p4, DOWN_UP, nENABLE, l_74155_decoder_1_p6, clock_1_out, l_74155_decoder_1_p5, ABCD, ABCD
  LED #(.active("false")) led_1 (.in(l_74155_decoder_1_p7));
  LED #(.active("false")) led_2 (.in(l_74155_decoder_1_p9));
  not not_1 (l_74191_counter_1_p4, button_1_out);
  LED #(.active("false")) led_3 (.in(l_74155_decoder_1_p11));
  LED #(.active("false")) led_4 (.in(l_74155_decoder_1_p13));
  Button button_1 (.out(button_1_out));
  LED #(.active("false")) led_5 (.in(l_74155_decoder_1_p8));
  LED #(.active("false")) led_6 (.in(l_74155_decoder_1_p10));
  LED #(.active("false")) led_7 (.in(l_74155_decoder_1_p12));
  LED #(.active("false")) led_8 (.in(l_74155_decoder_1_p14));

  // Notes on the sheet:
  //   CLOCK
  //   RESET
endmodule
