// Logisim project lab05.circ as structural Verilog: 2 circuits, main circuit pong_optimized
module pong_optimized (
);

  wire button_1_out, clock_1_out, l_74155_decoder_1_p1, l_74155_decoder_1_p3, l_74155_decoder_1_p5,
       l_74155_decoder_1_p6, l_74155_decoder_1_p7, l_74155_decoder_1_p8, l_74155_decoder_1_p9,
       l_74155_decoder_1_p10, l_74155_decoder_1_p11, l_74155_decoder_1_p12, l_74155_decoder_1_p13,
       l_74155_decoder_1_p14, l_74191_counter_1_p2, l_74191_counter_1_p5, l_74191_counter_1_p6, nand_1_out,
       nand_2_out, nand_3_out, not_1_out, not_2_out, not_3_out;

  // L_74155_decoder l_74155_decoder_1: pin names not known; wires that end beside it: l_74155_decoder_1_p1, l_74155_decoder_1_p1, l_74155_decoder_1_p3, l_74155_decoder_1_p3, l_74155_decoder_1_p5, l_74155_decoder_1_p6, l_74155_decoder_1_p7, l_74155_decoder_1_p8, l_74155_decoder_1_p9, l_74155_decoder_1_p10, l_74155_decoder_1_p11, l_74155_decoder_1_p12, l_74155_decoder_1_p13, l_74155_decoder_1_p14
  Clock clock_1 (.out(clock_1_out));
  LED #(.active("false")) led_1 (.in(l_74155_decoder_1_p7));
  // L_74191_counter l_74191_counter_1: pin names not known; wires that end beside it: 1'b0, l_74191_counter_1_p2, 1'b0, l_74155_decoder_1_p1, l_74191_counter_1_p5, l_74191_counter_1_p6, l_74155_decoder_1_p3, l_74155_decoder_1_p6, clock_1_out, l_74155_decoder_1_p5, 1'b0, 1'b0
  LED #(.active("false")) led_2 (.in(l_74155_decoder_1_p9));
  LED #(.active("false")) led_3 (.in(l_74155_decoder_1_p11));
  LED #(.active("false")) led_4 (.in(l_74155_decoder_1_p13));
  J_K_Flip_Flop j_k_ff_1 (
    .J(1'b1), .K(1'b1), .clk(button_1_out), .Q(l_74191_counter_1_p6), .reset(not_1_out));  // open: Qn, preset
  LED #(.active("false")) led_5 (.in(l_74155_decoder_1_p8));
  LED #(.active("false")) led_6 (.in(l_74155_decoder_1_p10));
  LED #(.active("false")) led_7 (.in(l_74155_decoder_1_p12));
  not not_1 (not_1_out, l_74191_counter_1_p5);
  LED #(.active("false")) led_8 (.in(l_74155_decoder_1_p14));
  nand nand_1 (nand_1_out, l_74155_decoder_1_p14, l_74155_decoder_1_p7);
  not not_2 (not_2_out, nand_1_out);
  Button button_1 (.out(button_1_out));
  Button #(.press("passive")) button_2 (.out(l_74191_counter_1_p5));
  nand nand_2 (nand_2_out, not_2_out, button_1_out);
  not not_3 (not_3_out, l_74191_counter_1_p2);
  J_K_Flip_Flop j_k_ff_2 (
    .J(1'b1), .K(1'b1), .clk(l_74191_counter_1_p5), .Qn(l_74155_decoder_1_p3), .reset(nand_3_out));  // open: Q, preset
  nand nand_3 (nand_3_out, nand_2_out, not_3_out);

  // Notes on the sheet:
  //   ABCD
  //   CLOCK
  //   PLAY
  //   RESET
endmodule

module pong_initial (
);

  wire button_1_out, clock_1_out, l_74155_decoder_1_p1, l_74155_decoder_1_p3, l_74155_decoder_1_p5,
       l_74155_decoder_1_p6, l_74155_decoder_1_p7, l_74155_decoder_1_p8, l_74155_decoder_1_p9,
       l_74155_decoder_1_p10, l_74155_decoder_1_p11, l_74155_decoder_1_p12, l_74155_decoder_1_p13,
       l_74155_decoder_1_p14, l_74191_counter_1_p2, l_74191_counter_1_p5, l_74191_counter_1_p6, nand_1_out,
       nand_2_out, nand_3_out, nand_4_out, nand_5_out, nor_1_out, nor_2_out, not_1_out, not_2_out, not_3_out,
       not_4_out;

  // L_74155_decoder l_74155_decoder_1: pin names not known; wires that end beside it: l_74155_decoder_1_p1, l_74155_decoder_1_p1, l_74155_decoder_1_p3, l_74155_decoder_1_p3, l_74155_decoder_1_p5, l_74155_decoder_1_p6, l_74155_decoder_1_p7, l_74155_decoder_1_p8, l_74155_decoder_1_p9, l_74155_decoder_1_p10, l_74155_decoder_1_p11, l_74155_decoder_1_p12, l_74155_decoder_1_p13, l_74155_decoder_1_p14
  Clock clock_1 (.out(clock_1_out));
  // L_74191_counter l_74191_counter_1: pin names not known; wires that end beside it: 1'b0, l_74191_counter_1_p2, 1'b0, l_74155_decoder_1_p1, l_74191_counter_1_p5, l_74191_counter_1_p6, l_74155_decoder_1_p3, l_74155_decoder_1_p6, clock_1_out, l_74155_decoder_1_p5, 1'b0, 1'b0
  LED #(.active("false")) led_1 (.in(l_74155_decoder_1_p7));
  LED #(.active("false")) led_2 (.in(l_74155_decoder_1_p9));
  LED #(.active("false")) led_3 (.in(l_74155_decoder_1_p11));
  LED #(.active("false")) led_4 (.in(l_74155_decoder_1_p13));
  not not_1 (not_1_out, l_74155_decoder_1_p7);
  LED #(.active("false")) led_5 (.in(l_74155_decoder_1_p8));
  LED #(.active("false")) led_6 (.in(l_74155_decoder_1_p10));
  LED #(.active("false")) led_7 (.in(l_74155_decoder_1_p12));
  nand nand_1 (nand_1_out, not_1_out, button_1_out);
  nand nand_2 (nand_2_out, button_1_out, not_2_out);
  nand nand_3 (nand_3_out, nand_1_out, nand_2_out);
  LED #(.active("false")) led_8 (.in(l_74155_decoder_1_p14));
  Button button_1 (.out(button_1_out));
  not not_2 (not_2_out, l_74155_decoder_1_p14);
  J_K_Flip_Flop j_k_ff_1 (
    .J(1'b1), .K(1'b1), .clk(nand_3_out), .Q(l_74191_counter_1_p6), .reset(not_3_out));  // open: Qn, preset
  Button #(.press("passive")) button_2 (.out(l_74191_counter_1_p5));
  not not_3 (not_3_out, l_74191_counter_1_p5);
  J_K_Flip_Flop j_k_ff_2 (
    .J(1'b1), .K(1'b1), .clk(l_74191_counter_1_p5), .Qn(l_74155_decoder_1_p3), .reset(not_4_out));  // open: Q, preset
  nand nand_4 (nand_4_out, button_1_out, l_74155_decoder_1_p14);
  nand nand_5 (nand_5_out, button_1_out, l_74155_decoder_1_p7);
  not not_4 (not_4_out, nor_1_out);
  nor nor_1 (nor_1_out, nor_2_out, l_74191_counter_1_p2);
  nor nor_2 (nor_2_out, nand_4_out, nand_5_out);

  // Notes on the sheet:
  //   ABCD
  //   CLOCK
  //   PLAY
  //   RESET
endmodule
